# Fritzing sketch MeetingSignal (saved by Fritzing 0.9.5d)

parts:
  U1 = ESP32-38PinWide [part_number=ESP32-38PinWide]
  TP1 = TP4056 [chip_label=TP4056 package="DIP (Dual Inline) [THT]"]
  LED2 = Super Flux LED blue [color=Yellow]
  R1 = Resistor [tolerance=±5% resistance=100k package=THT]
  U2 = LIPO-1000mAh [package=lipo-1000]
  LED1 = Super Flux LED blue [color=White]
  LED3 = Super Flux LED blue [color=White]  # not connected
  LED4 = Super Flux LED blue [color=White]  # not connected
  LED6 = Super Flux LED blue [color=Yellow]  # not connected
  LED7 = Super Flux LED blue [color=Yellow]  # not connected
  S1 = Taiway 100-SP-X-T1 SPDT Miniature Toggle Switch [part_number=100-SP-X-T1-0-0-B1-M1 package=THT]
  R2 = Resistor [tolerance=±5% resistance=100k package=THT]  # not connected

nets:
  N1: U1.GPIO36, R1.Pin_1
  N2: U1.GPIO13, LED2.anode
  N3: U1.GPIO9, U1.GND, LED1.cathode
  N4: U1.GPIO11, TP1.pin6
  N5: U1.VIN, S1.L2
  N6: TP1.pin3, S1.L1
  N7: TP1.pin4, U2.+
  N8: TP1.pin5, U2.-

notes:
  My led strip has GND and 2 5V inputs to turn on warm white or cold white leds independently

custom parts:
  ESP32-38PinWide: Generic 38-Pin ESP32 with wide format (only access to one side of pins on a breadboard) based on Stephen Lilley's HiLetgo ESP-WROOM-32 ESP32 ESP-32S Development Board.
  TP4056: A DIP stand-in part for whatever IC you want. With 6 pins on a 300mil dual inline package (DIP) footprint.
